# Fritzing sketch Diagrama (saved by Fritzing 0.9.3b)
breadboards: 1

parts:
  A1 = DHT22 module
  WeMos_D1_Mini1 = WeMos D1 Mini  # not connected
  Mod1 = SDS011 - dust sensor [part_number=1]

nets:
  N1: A1.-, Mod1.GND

custom parts:
  DHT22 module: DHT22 module. Pins VCC Data GND.
  SDS011 - dust sensor: The SDS 011 Sensor is a quite recent Air Quality Sensor developed by inovafit, a spin-off from the university of Jinan (in Shandong). With its size, it is probably one of the best sensor in terms of accuracy: While other sensors tend to focus on shrinking the sensor size, the SDS 011 has opted for a size tradeoff allowing it to use a larger fan. And the larger the fan, the better the quality.
